# Fritzing sketch smart-o-harp (saved by Fritzing 0.9.3b)
breadboards: 3

parts:
  Part1 = Arduino Uno (Rev3)
  IC1 = IC, SIP package, 8 pins [chip_label="12 buttons"]
  Power_plug1 = Power plug
  IC2 = SHIFT REGISTER [package=dil16]
  R2 = Resistor [tolerance=±5% resistance=10k package="2010 [SMD]"]
  R3 = Resistor [tolerance=±5% resistance=10k package="2010 [SMD]"]
  R4 = Resistor [tolerance=±5% resistance=10k package="2010 [SMD]"]
  R5 = Resistor [tolerance=±5% resistance=10k package="2010 [SMD]"]
  R6 = Resistor [tolerance=±5% resistance=10k package="2010 [SMD]"]
  R7 = Resistor [tolerance=±5% resistance=10k package="2010 [SMD]"]
  Q12 = NPN-Transistor [package="TO92 [THT]"]
  Q13 = NPN-Transistor [package="TO92 [THT]"]
  Q14 = NPN-Transistor [package="TO92 [THT]"]
  Q15 = NPN-Transistor [package="TO92 [THT]"]
  Q16 = NPN-Transistor [package="TO92 [THT]"]
  Q17 = NPN-Transistor [package="TO92 [THT]"]
  Q18 = NPN-Transistor [package="TO92 [THT]"]
  Q19 = NPN-Transistor [package="TO92 [THT]"]
  Q20 = NPN-Transistor [package="TO92 [THT]"]
  Q21 = NPN-Transistor [package="TO92 [THT]"]
  R9 = Resistor [tolerance=±5% resistance=10k package="2010 [SMD]"]
  R10 = Resistor [tolerance=±5% resistance=10k package="2010 [SMD]"]
  R11 = Resistor [tolerance=±5% resistance=10k package="2010 [SMD]"]
  R12 = Resistor [tolerance=±5% resistance=10k package="2010 [SMD]"]
  L1 = Solenoid
  L2 = Solenoid
  L3 = Solenoid
  IC3 = SHIFT REGISTER [package=dil16]
  Q22 = NPN-Transistor [package="TO92 [THT]"]
  Q23 = NPN-Transistor [package="TO92 [THT]"]
  R13 = Resistor [tolerance=±5% resistance=10k package="2010 [SMD]"]
  R14 = Resistor [tolerance=±5% resistance=10k package="2010 [SMD]"]
  L4 = Solenoid
  L5 = Solenoid
  L6 = Solenoid
  L7 = Solenoid
  L8 = Solenoid
  L9 = Solenoid
  L10 = Solenoid
  L11 = Solenoid
  L12 = Solenoid
  D1 = Rectifier Diode [part_number=1N4001 package="300 mil [THT]"]
  D2 = Rectifier Diode [part_number=1N4001 package="300 mil [THT]"]
  D3 = Rectifier Diode [part_number=1N4001 package="300 mil [THT]"]
  D4 = Rectifier Diode [part_number=1N4001 package="300 mil [THT]"]
  D5 = Rectifier Diode [part_number=1N4001 package="300 mil [THT]"]
  D6 = Rectifier Diode [part_number=1N4001 package="300 mil [THT]"]
  D7 = Rectifier Diode [part_number=1N4001 package="300 mil [THT]"]
  D8 = Rectifier Diode [part_number=1N4001 package="300 mil [THT]"]
  D9 = Rectifier Diode [part_number=1N4001 package="300 mil [THT]"]
  D10 = Rectifier Diode [part_number=1N4001 package="300 mil [THT]"]
  D11 = Rectifier Diode [part_number=1N4001 package="300 mil [THT]"]
  D12 = Rectifier Diode [part_number=1N4001 package="300 mil [THT]"]

nets:
  N1: Part1.D8, IC2.RCK, IC3.RCK
  N2: Part1.D11_PWM/MOSI, IC2.SER
  VCC: Part1.D12/MISO, IC2.SCK, IC2.VCC, R10.Pin_0, IC3.SCL, IC3.SCK, IC3.VCC
  GND: Part1.GND, IC1.pin8, Power_plug1.GND, IC2.GND, IC2.G, Q12.E, Q13.E, Q13.C, Q14.E, Q15.E, Q16.E, Q17.E, Q18.E, Q19.E, Q20.E, Q21.E, L2.pin1, IC3.GND, IC3.G, Q22.E, Q23.E, D11.anode
  N3: Part1.D0/RX, IC1.pin7
  N4: Part1.D2, IC1.pin6
  N5: Part1.D3_PWM, IC1.pin5
  N6: Part1.D4, IC1.pin4
  N7: Part1.D5_PWM, IC1.pin3
  N8: Part1.D6_PWM, IC1.pin2
  N9: Part1.D7, IC1.pin1
  VIN: Part1.VIN, Power_plug1.VCC, L1.pin2, L2.pin2, L3.pin2, L4.pin2, L5.pin2, L6.pin2, L7.pin2, L8.pin2, L9.pin2, L10.pin2, L11.pin2, L12.pin2, D1.cathode, D2.cathode, D3.cathode, D4.cathode, D5.cathode, D6.cathode, D7.cathode, D8.cathode, D9.cathode, D10.cathode, D11.cathode, D12.cathode
  N10: IC2.QB, R12.Pin_0
  N11: IC2.QC, R6.Pin_0
  N12: IC2.QD, R7.Pin_0
  N13: IC2.QE, R4.Pin_0
  N14: IC2.QF, R5.Pin_0
  N15: IC2.QG, R3.Pin_0
  N16: IC2.QH, R2.Pin_0
  N17: IC2.QH*, IC3.SER
  N18: R2.Pin_1, Q12.B
  N19: R3.Pin_1, Q13.B
  N20: R4.Pin_1, Q17.B
  N21: R5.Pin_1, Q14.B
  N22: R6.Pin_1, Q16.B
  N23: R7.Pin_1, Q15.B
  N24: Q12.C, L1.pin1, D12.anode
  N25: Q14.C, L3.pin1, D10.anode
  N26: Q15.C, L4.pin1, D8.anode
  N27: Q16.C, L6.pin1, D7.anode
  N28: Q17.C, L5.pin1, D9.anode
  N29: Q18.B, R12.Pin_1
  N30: Q18.C, L7.pin1, D6.anode
  N31: Q19.B, R9.Pin_1
  N32: Q19.C, L9.pin1, D4.anode
  N33: Q20.B, R11.Pin_1
  N34: Q20.C, L10.pin1, D3.anode
  N35: Q21.B, R10.Pin_1
  N36: Q21.C, L8.pin1, D5.anode
  N37: R9.Pin_0, IC3.QH
  N38: R11.Pin_0, IC3.QG
  N39: IC3.QE, R13.Pin_0
  N40: IC3.QF, R14.Pin_0
  N41: Q22.B, R14.Pin_1
  N42: Q22.C, L11.pin1, D2.anode
  N43: Q23.B, R13.Pin_1
  N44: Q23.C, L12.pin1, D1.anode

notes:
  Solenoids: 12V DC spring push/pull 4mm.
  From experimentation, requires at least 70 mA to budge, draws about 130 mA if it can.
  12V 5A power supply
  Red wires at 12V
  Orange wires at 5V from arduino.
  Black wires are shared ground.
  The diodes prevent backwards current dischange when the solenoids turn off.
  12 outpus used.
  4 outputs unused.
  Keypad wiring entirely separate from the rest of the circuit
  Power rail on this board: 5V
  12 Button keypad (grounded) right here
  UNO used for experimental staging. Should be able to drop a Nano into the final project.
  2 8-bit shift registers in series
